// Logisim project LC3-2200a.circ as structural Verilog
module Datapath (
  input  in_1,
  input  in_2,
  input  in_3,
  input  in_4,
  input  in_5,
  input  in_6,
  input  in_7,
  input  in_8,
  input  in_9,
  input  in_10,
  input  [1:0] in_11,
  input  in_12,
  input  in_13,
  input  [3:0] in_14,
  input  in_15,
  input  in_16,
  input  in_17
);

  wire A, comparator_1_eq, comparator_1_gt, comparator_1_lt, D;
  wire [3:0] DR, OP, SR1, SR2;
  wire [17:4] IR_q;
  wire [31:0] A_q, alu_1_out, B_q, bit_extender_1_out, controlled_buffer_1_out, MAR_q, PC_q, ram_1_data,
       ram_2_data;

  Register #(.width(32)) PC (.D(controlled_buffer_1_out), .en(in_2), .Q(PC_q));  // open: clk, clr
  assign controlled_buffer_1_out = in_1 ? PC_q : 32'bz;  // Controlled_Buffer controlled_buffer_1
  Comparator #(.width(32), .mode("unsigned")) comparator_1 (
    .a(controlled_buffer_1_out), .b({32{1'b0}}), .gt(comparator_1_gt), .eq(comparator_1_eq),
    .lt(comparator_1_lt));
  Register #(.width(32)) u_A (.D(controlled_buffer_1_out), .en(in_6), .Q(A_q));  // open: clk, clr
  ALU alu_1 (.A(A_q), .B(B_q), .Out(alu_1_out), .Func(in_11));
  assign controlled_buffer_1_out = in_5 ? alu_1_out : 32'bz;  // Controlled_Buffer controlled_buffer_2
  Register #(.width(32)) B (.D(controlled_buffer_1_out), .en(in_10), .Q(B_q));  // open: clk, clr
  Register #(.width(32)) MAR (.D(controlled_buffer_1_out), .en(in_13), .Q(MAR_q));  // open: clk, clr
  RAM #(.addrWidth(4), .dataWidth(32), .bus("separate")) ram_1 (
    .addr(in_14), .din(controlled_buffer_1_out), .data(ram_1_data), .str(in_7));  // open: sel, clk, ld, clr
  assign controlled_buffer_1_out = in_9 ? ram_1_data : 32'bz;  // Controlled_Buffer controlled_buffer_3
  Clock clock_1 ();  // open: out
  Register #(.width(32)) IR (
    .D(controlled_buffer_1_out), .en(in_16), .Q({OP, DR, SR1, A, D, IR_q, SR2}));  // open: clk, clr
  RAM #(.addrWidth(24), .dataWidth(32), .bus("separate")) ram_2 (
    .addr(MAR_q[31:8]), .din(controlled_buffer_1_out), .data(ram_2_data), .str(in_3));  // open: sel, clk, ld, clr
  assign controlled_buffer_1_out = in_12 ? ram_2_data : 32'bz;  // Controlled_Buffer controlled_buffer_4
  Bit_Extender #(.in_width(20), .out_width(32), .\type ("input")) bit_extender_1 (
    .in({A, D, IR_q, SR2}), .out(bit_extender_1_out));  // open: extend
  assign controlled_buffer_1_out = in_15 ? bit_extender_1_out : 32'bz;  // Controlled_Buffer controlled_buffer_5

  // Other names for the same wires on the sheet: ChkCC = in_8; DrALU = in_5; DrMem = in_12; DrOff = in_15;
  //   DrPC = in_1; DrReg = in_9; Func[1:0] = in_11; LdA = in_6; LdB = in_10; LdCC = in_17; LdIR = in_16;
  //   LdMAR = in_13; LdPC = in_2; OpTest = in_4; RegSel[3:0] = in_14; WrMem = in_3; WrReg = in_7
endmodule

module ALU (
  input  [31:0] A,
  input  [31:0] B,
  input  [1:0] Func,
  output [31:0] Out
);
endmodule
