// Logisim project li_zhijian.circ as structural Verilog
module main (
);

  wire A, CLK, comparator_1_eq, D, Use_IMM;
  wire [1:0] Func, undriven;
  wire [3:0] if_idrr_buffer_1_ry_out, if_idrr_buffer_1_rz_out, OP, RX;
  wire [17:0] if_idrr_buffer_1_imm_out;
  wire [31:0] adder_1_out, adder_2_out, alu_1_out, bit_extender_1_out, i_mem_1_ir_out,
       idrr_ex_buffer_1_a_out, idrr_ex_buffer_1_b_out, idrr_ex_buffer_1_imm_out, idrr_ex_buffer_1_result_out,
       if_idrr_buffer_1_pc_out, multiplexer_1_out, multiplexer_2_out, PC_q, regs_1_a, regs_1_b;

  Clock CLOCK (.out(CLK));
  Adder #(.width(32)) adder_1 (.a(PC_q), .b(32'h1), .out(adder_1_out));  // open: cin, cout
  I_MEM i_mem_1 (.PC_IN(PC_q), .IR_OUT(i_mem_1_ir_out), .in_1(CLK));
  Register #(.width(32)) PC (.D(multiplexer_1_out), .Q(PC_q), .clk(CLK));  // open: en, clr
  Multiplexer #(.select(2), .width(32), .enable("false")) multiplexer_1 (
    .in0(adder_1_out), .out(multiplexer_1_out), .sel(undriven));  // open: in1, in2, in3
  IF_IDRR_Buffer if_idrr_buffer_1 (
    .in_1(CLK), .PC_N(adder_1_out), .IR_IN(i_mem_1_ir_out), .PC_OUT(if_idrr_buffer_1_pc_out), .OP_OUT(OP),
    .RX_OUT(RX), .RY_OUT(if_idrr_buffer_1_ry_out), .RZ_OUT(if_idrr_buffer_1_rz_out),
    .IMM_OUT({A, D, if_idrr_buffer_1_imm_out}));
  Regs regs_1 (
    .OP_IN(OP), .RX_IN(RX), .RY_IN(if_idrr_buffer_1_ry_out), .RZ_IN(if_idrr_buffer_1_rz_out), .CK(CLK),
    .A(regs_1_a), .B(regs_1_b), .Use_IMM(Use_IMM), .Func(Func));  // open: BEQ, JALR, LDR, STR, BR
  assign bit_extender_1_out = {{12{A}}, {A, D, if_idrr_buffer_1_imm_out}};  // Bit_Extender bit_extender_1
  // AND_Gate and_1 has open pins: in1=comparator_1_eq, out=open
  Comparator #(.width(32)) comparator_1 (.a(regs_1_a), .b(regs_1_b), .eq(comparator_1_eq));  // open: gt, lt
  Adder #(.width(32)) adder_2 (
    .a(bit_extender_1_out), .b(if_idrr_buffer_1_pc_out), .out(adder_2_out));  // open: cin, cout
  IDRR_EX_Buffer idrr_ex_buffer_1 (
    .CLK(CLK), .IMM_IN(bit_extender_1_out), .Result_IN(adder_2_out), .A_IN(regs_1_a), .B_IN(regs_1_b),
    .IMM_OUT(idrr_ex_buffer_1_imm_out), .Result_OUT(idrr_ex_buffer_1_result_out),
    .A_OUT(idrr_ex_buffer_1_a_out), .B_OUT(idrr_ex_buffer_1_b_out), .OP_IN(OP), .RX_IN(RX));  // open: Cond_IN, Cond_OUT, OP_OUT, RX_OUT
  ALU alu_1 (.A(idrr_ex_buffer_1_a_out), .B(multiplexer_2_out), .Out(alu_1_out), .A_2(A), .D(D), .Func(Func));
  Multiplexer #(.width(32), .enable("false")) multiplexer_2 (
    .in0(idrr_ex_buffer_1_b_out), .in1(idrr_ex_buffer_1_imm_out), .out(multiplexer_2_out), .sel(Use_IMM));
endmodule

module Dual_Ported_Register_File (
  input  CLK,
  input  WrEN,
  input  [3:0] WrREGNO,
  input  [3:0] RdREGNO1,
  input  [3:0] RdREGNO2,
  input  [31:0] INPUT,
  output [31:0] OUT1,
  output [31:0] OUT2
);

  wire En_a0, En_a1, En_a2, En_at, En_fp, En_k0, En_ra, En_s0, En_s1, En_s2, En_sp, En_t0, En_t1, En_t2,
       En_v0;
  wire [31:0] a0, a1, a2, at, fp, k0, ra, s0, s1, s2, sp, t0, t1, t2, v0, zero;

  Decoder #(.select(4), .disabled(0)) decoder_1 (
    .out1(En_at), .out2(En_v0), .out3(En_a0), .out4(En_a1), .out5(En_a2), .out6(En_t0), .out7(En_t1),
    .out8(En_t2), .out9(En_s0), .out10(En_s1), .out11(En_s2), .out12(En_k0), .out13(En_sp), .out14(En_fp),
    .out15(En_ra), .sel(WrREGNO), .en(WrEN));  // open: out0
  Register #(.width(32)) u_zero (.D(INPUT), .en(1'b0), .Q(zero), .clk(CLK));  // open: clr
  Register #(.width(32)) u_at (.D(INPUT), .en(En_at), .Q(at), .clk(CLK));  // open: clr
  Register #(.width(32)) u_v0 (.D(INPUT), .en(En_v0), .Q(v0), .clk(CLK));  // open: clr
  Register #(.width(32)) u_a0 (.D(INPUT), .en(En_a0), .Q(a0), .clk(CLK));  // open: clr
  Register #(.width(32)) u_a1 (.D(INPUT), .en(En_a1), .Q(a1), .clk(CLK));  // open: clr
  Register #(.width(32)) u_a2 (.D(INPUT), .en(En_a2), .Q(a2), .clk(CLK));  // open: clr
  Register #(.width(32)) u_t0 (.D(INPUT), .en(En_t0), .Q(t0), .clk(CLK));  // open: clr
  Register #(.width(32)) u_t1 (.D(INPUT), .en(En_t1), .Q(t1), .clk(CLK));  // open: clr
  Multiplexer #(.select(4), .width(32), .disabled(0), .enable("false")) multiplexer_1 (
    .in0(zero), .in1(at), .in2(v0), .in3(a0), .in4(a1), .in5(a2), .in6(t0), .in7(t1), .in8(t2), .in9(s0),
    .in10(s1), .in11(s2), .in12(k0), .in13(sp), .in14(fp), .in15(ra), .out(OUT2), .sel(RdREGNO2));
  Register #(.width(32)) u_t2 (.D(INPUT), .en(En_t2), .Q(t2), .clk(CLK));  // open: clr
  Register #(.width(32)) u_s0 (.D(INPUT), .en(En_s0), .Q(s0), .clk(CLK));  // open: clr
  Register #(.width(32)) u_s1 (.D(INPUT), .en(En_s1), .Q(s1), .clk(CLK));  // open: clr
  Register #(.width(32)) u_s2 (.D(INPUT), .en(En_s2), .Q(s2), .clk(CLK));  // open: clr
  Register #(.width(32)) u_k0 (.D(INPUT), .en(En_k0), .Q(k0), .clk(CLK));  // open: clr
  Register #(.width(32)) u_sp (.D(INPUT), .en(En_sp), .Q(sp), .clk(CLK));  // open: clr
  Register #(.width(32)) u_fp (.D(INPUT), .en(En_fp), .Q(fp), .clk(CLK));  // open: clr
  Register #(.width(32)) u_ra (.D(INPUT), .en(En_ra), .Q(ra), .clk(CLK));  // open: clr
  Multiplexer #(.select(4), .width(32), .disabled(0), .enable("false")) multiplexer_2 (
    .in0(zero), .in1(at), .in2(v0), .in3(a0), .in4(a1), .in5(a2), .in6(t0), .in7(t1), .in8(t2), .in9(s0),
    .in10(s1), .in11(s2), .in12(k0), .in13(sp), .in14(fp), .in15(ra), .out(OUT1), .sel(RdREGNO1));

  // Notes on the sheet:
  //   MODIFY AT YOUR OWN RISK
endmodule

module IF_IDRR_Buffer (
  input  in_1,
  input  [31:0] PC_N,
  input  [31:0] IR_IN,
  output [31:0] PC_OUT,
  output [3:0] OP_OUT,
  output [3:0] RX_OUT,
  output [3:0] RY_OUT,
  output [3:0] RZ_OUT,
  output [19:0] IMM_OUT
);

  Register #(.width(32)) PC (.D(PC_N), .Q(PC_OUT), .clk(in_1));  // open: en, clr
  Register #(.width(32)) IR (.D(IR_IN), .Q({OP_OUT, RX_OUT, RY_OUT, IMM_OUT}), .clk(in_1));  // open: en, clr

  assign RZ_OUT = IMM_OUT[3:0];

  // Other names for the same wires on the sheet: CLK = in_1
endmodule

module IDRR_EX_Buffer (
  input  CLK,
  input  [3:0] OP_IN,
  input  [3:0] RX_IN,
  input  [31:0] IMM_IN,
  input  [31:0] Result_IN,
  input  [31:0] A_IN,
  input  [31:0] B_IN,
  input  Cond_IN,
  output [3:0] OP_OUT,
  output [3:0] RX_OUT,
  output [31:0] IMM_OUT,
  output [31:0] Result_OUT,
  output [31:0] A_OUT,
  output [31:0] B_OUT,
  output Cond_OUT
);

  Register #(.width(4)) register_1 (.D(OP_IN), .Q(OP_OUT), .clk(CLK));  // open: en, clr
  Register #(.width(4)) register_2 (.D(RX_IN), .Q(RX_OUT), .clk(CLK));  // open: en, clr
  Register #(.width(32)) register_3 (.D(IMM_IN), .Q(IMM_OUT), .clk(CLK));  // open: en, clr
  Register #(.width(32)) register_4 (.D(Result_IN), .Q(Result_OUT), .clk(CLK));  // open: en, clr
  Register #(.width(32)) register_5 (.D(A_IN), .Q(A_OUT), .clk(CLK));  // open: en, clr
  Register #(.width(32)) register_6 (.D(B_IN), .Q(B_OUT), .clk(CLK));  // open: en, clr
  Register #(.width(1)) register_7 (.D(Cond_IN), .Q(Cond_OUT), .clk(CLK));  // open: en, clr
endmodule

module I_MEM (
  input  in_1,
  input  [31:0] PC_IN,
  output [31:0] IR_OUT
);

  RAM #(.addrWidth(24), .dataWidth(32)) ram_1 (
    .addr(PC_IN[23:0]), .data(IR_OUT), .clk(in_1), .ld(1'b1));  // open: sel, clr

  // Other names for the same wires on the sheet: CLK = in_1
endmodule

module Regs (
  input  CK,
  input  [3:0] OP_IN,
  input  [3:0] RX_IN,
  input  [3:0] RY_IN,
  input  [3:0] RZ_IN,
  output [31:0] A,
  output [31:0] B,
  output Use_IMM,
  output [1:0] Func,
  output BR,
  output BEQ,
  output JALR,
  output LDR,
  output STR
);

  wire Use_RZ;
  wire [3:0] multiplexer_1_out;

  Multiplexer #(.width(4), .enable("false")) multiplexer_1 (
    .in0(RX_IN), .in1(RZ_IN), .out(multiplexer_1_out), .sel(Use_RZ));
  Dual_Ported_Register_File dual_ported_register_file_1 (
    .CLK(CK), .WrREGNO(RX_IN), .RdREGNO1(RY_IN), .RdREGNO2(multiplexer_1_out), .OUT1(A), .OUT2(B));  // open: INPUT, WrEN
  ROM #(.addrWidth(4), .dataWidth(9)) rom_1 (
    .addr(OP_IN), .data({Use_RZ, Use_IMM, Func, BR, BEQ, JALR, LDR, STR}));  // open: sel

  // Other names for the same wires on the sheet: CLK = CK; OP[3:0] = OP_IN; RX[3:0] = RX_IN; RY[3:0] = RY_IN;
  //   RZ[3:0] = RZ_IN
endmodule

module ALU (
  input  [31:0] A,
  input  [31:0] B,
  input  A_2,
  input  D,
  input  [1:0] Func,
  output [31:0] Out
);

  wire [31:0] adder_1_out, adder_2_out, multiplexer_1_out, nand_1_out, shifter_1_out, shifter_2_out,
       shifter_3_out;

  Shifter #(.width(32)) shifter_1 (.in(A), .\dist (B[4:0]), .out(shifter_1_out));
  Shifter #(.width(32), .shift("lr")) shifter_2 (.in(A), .\dist (B[4:0]), .out(shifter_2_out));
  Shifter #(.width(32), .shift("ar")) shifter_3 (.in(A), .\dist (B[4:0]), .out(shifter_3_out));
  Adder #(.width(32)) adder_1 (.a(A), .b(B), .out(adder_1_out));  // open: cin, cout
  assign nand_1_out = ~(A & B);  // NAND_Gate nand_1, 32 bits wide
  Adder #(.width(32)) adder_2 (.a(A), .b(32'h1), .out(adder_2_out));  // open: cin, cout
  Multiplexer #(.select(2), .width(32), .disabled(0), .enable("false")) multiplexer_1 (
    .in0(shifter_1_out), .in1(shifter_2_out), .in2(shifter_1_out), .in3(shifter_3_out),
    .out(multiplexer_1_out), .sel({A_2, D}));
  Multiplexer #(.select(2), .width(32), .disabled(0), .enable("false")) multiplexer_2 (
    .in0(adder_1_out), .in1(nand_1_out), .in2(adder_2_out), .in3(multiplexer_1_out), .out(Out), .sel(Func));
endmodule

module IF (
  input  CLK,
  input  JALR,
  input  [31:0] PC___Off,
  input  [31:0] JALR_PC,
  input  BR,
  output [31:0] PC_OUT,
  output [31:0] IR_OUT
);

  wire [31:0] multiplexer_1_out, PC_q;

  Adder #(.width(32)) adder_1 (.a(PC_q), .b(32'h1), .out(PC_OUT));  // open: cin, cout
  I_MEM i_mem_1 (.PC_IN(PC_q), .IR_OUT(IR_OUT), .in_1(CLK));
  Register #(.width(32)) PC (.D(multiplexer_1_out), .Q(PC_q), .clk(CLK));  // open: en, clr
  Multiplexer #(.select(2), .width(32), .enable("false")) multiplexer_1 (
    .in0(PC_OUT), .in1(PC___Off), .in2(JALR_PC), .in3(JALR_PC), .out(multiplexer_1_out), .sel({JALR, BR}));
endmodule

module ID (
  input  [3:0] OP_IN,
  input  [19:0] IMM_IN,
  input  [3:0] RX_IN,
  input  [31:0] PC_IN,
  input  [3:0] RY_IN,
  input  [3:0] RZ_IN
);

  wire A, D, undriven_6;
  wire [3:0] RX, undriven, undriven_2, undriven_3;
  wire [17:0] undriven_4;
  wire [31:0] adder_1_out, bit_extender_1_out, regs_1_a, regs_1_b, undriven_5;

  Regs regs_1 (
    .OP_IN(undriven), .RX_IN(RX), .RY_IN(undriven_2), .RZ_IN(undriven_3), .CK(undriven_6), .A(regs_1_a),
    .B(regs_1_b));  // open: Use_IMM, Func, BEQ, JALR, LDR, STR, BR
  assign bit_extender_1_out = {{12{A}}, {A, D, undriven_4}};  // Bit_Extender bit_extender_1
  Adder #(.width(32)) adder_1 (.a(bit_extender_1_out), .b(undriven_5), .out(adder_1_out));  // open: cin, cout
endmodule
